# Fritzing sketch not-test (saved by Fritzing 0.9.3b)
breadboards: 1

parts:
  Part1 = Adafruit Micro USB Breakout [part_number="Adafruit #1833"]
  S2 = Pushbutton [package="[THT]"]
  R2 = Resistor [tolerance=±5% resistance=1k package=THT]
  IC1 = 7404 [package="DIP (Dual Inline) [THT]"]
  LED1 = LED - 3mm [color="Red (633nm)" package="3 mm [THT]"]
  LED6 = LED - 3mm [color="Red (633nm)" package="3 mm [THT]"]
  LED3 = LED - 3mm [color="Red (633nm)" package="3 mm [THT]"]
  LED4 = LED - 3mm [color="Red (633nm)" package="3 mm [THT]"]
  LED7 = LED - 3mm [color="Red (633nm)" package="3 mm [THT]"]
  LED5 = LED - 3mm [color="Red (633nm)" package="3 mm [THT]"]

nets:
  GND: Part1.GND, R2.Pin_1, IC1.GND, LED1.cathode, LED6.cathode, LED3.cathode, LED4.cathode, LED7.cathode, LED5.cathode
  N1: Part1.VBUS, S2.Pin_3, S2.Pin_4, IC1.VCC
  N2: S2.Pin_1, S2.Pin_2, R2.Pin_0, IC1.1A, IC1.2A, IC1.3A, IC1.4A, IC1.5A, IC1.6A
  N3: IC1.1Y, LED1.anode
  N4: IC1.2Y, LED5.anode
  N5: IC1.3Y, LED6.anode
  N6: IC1.4Y, LED7.anode
  N7: IC1.5Y, LED4.anode
  N8: IC1.6Y, LED3.anode

custom parts:
  Adafruit Micro USB Breakout: Simple but effective - this breakout board has a USB Micro-B connector, with all 5 pins broken out. Great for pairing with a microcontroller with USB support, or adding USB 5V power to a project. We use a micro-AB connector with through-hole shielding pads for an excellent strong connection - it won't rip off by accident! Comes with one fully assembled and tested micro B breakout PCB and a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
  7404: Hex inverter
